// Digital circuit Adder and Logic Circuit.dig as structural Verilog
module Adder_and_Logic_Circuit (
  input  [15:0] AC,
  input  [15:0] DR,
  input  [7:0] INPR,
  input  [6:0] AL_OP,
  input  E,
  output [15:0] OUT,
  output C_out
);

  wire add_1_c_o;
  wire [15:0] add_1_s, and_2_out, and_3_out, and_4_out, and_5_out, and_6_out, and_7_out, and_8_out,
       not_1_out, or_1_out, or_2_out;

  Add #(.Bits(16)) add_1 (.a(AC), .b(DR), .c_i(1'b0), .s(add_1_s), .c_o(add_1_c_o));
  and and_1 (C_out, add_1_c_o, AL_OP[1]);
  assign not_1_out = ~AC;  // Not not_1, 16 bits wide
  assign and_2_out = {16{AL_OP[0]}} & AC & DR;  // And and_2, 16 bits wide
  assign and_3_out = {16{AL_OP[1]}} & add_1_s;  // And and_3, 16 bits wide
  assign and_4_out = {16{AL_OP[2]}} & DR;  // And and_4, 16 bits wide
  assign and_5_out = {16{AL_OP[3]}} & {{8{1'b0}}, INPR};  // And and_5, 16 bits wide
  assign and_6_out = {16{AL_OP[4]}} & not_1_out;  // And and_6, 16 bits wide
  assign and_7_out = {16{AL_OP[5]}} & {E, AC[15:1]};  // And and_7, 16 bits wide
  assign and_8_out = {16{AL_OP[6]}} & {AC[14:0], E};  // And and_8, 16 bits wide
  assign or_1_out = and_2_out | and_3_out | and_4_out | and_5_out;  // Or or_1, 16 bits wide
  assign or_2_out = and_6_out | and_7_out | and_8_out;  // Or or_2, 16 bits wide
  assign OUT = or_1_out | or_2_out;  // Or or_3, 16 bits wide

  // Other names for the same wires on the sheet: AC_shl[15:0] = {AC[14:0], E}; AC_shr[15:0] = {E, AC[15:1]};
  //   AL_OP_16_AND[15:0] = {16{AL_OP[0]}}; AL_OP_AND = AL_OP[0]; AL_OP_16_ADD[15:0] = {16{AL_OP[1]}};
  //   AL_OP_ADD = AL_OP[1]; AL_OP_16_DR[15:0] = {16{AL_OP[2]}}; AL_OP_DR = AL_OP[2];
  //   AL_OP_16_INPR[15:0] = {16{AL_OP[3]}}; AL_OP_INPR = AL_OP[3]; AL_OP_16_COM[15:0] = {16{AL_OP[4]}};
  //   AL_OP_COM = AL_OP[4]; AL_OP_16_SHR[15:0] = {16{AL_OP[5]}}; AL_OP_SHR = AL_OP[5];
  //   AL_OP_16_SHL[15:0] = {16{AL_OP[6]}}; AL_OP_SHL = AL_OP[6]; INPR16bits[7:0] = INPR

  // Notes on the sheet:
  //   AC SHR
  //   AC SHL
  //   Fig. 5.21
endmodule

/* Test case:
AC	DR	INPR	AL-OP		OUT	C_out
0	0	0	0x0		0	0
1000	2000	0	2		3000	0		#1000+2000=3000
65500	36	0	2		0	1		#Addition overflow
65500	37	0	2		1	1		#Addition overflow
0x5555	0xFFFF	0	1		0x5555	0		#AND test
0x5555	0xA050	0	1		0x0050	0		#AND test
0x5555	0x1234	0	4		0x1234	0		#DR pass through
0x5555	0x1234	0x70	8		0x0070	0		#INPR pass through
0x5555	0x1234	0x70	16		0xAAAA	0		#Complement AC
0x5555	0x1234	0x70	32		0x2AAA	0		#SHR AC
0x5555	0x1234	0x70	64		0xAAAA	0		#SHL AC
*/
