// Digital circuit AlphanumericInstructionDecoderIC.dig as structural Verilog
module AlphanumericInstructionDecoderIC (
  input  [15:0] IR,
  output [15:0] Letter1,
  output [15:0] Letter2,
  output [15:0] Letter3,
  output Indirect,
  output Digit1A,
  output Digit1B,
  output Digit1C,
  output Digit1D,
  output Digit2A,
  output Digit2B,
  output Digit2C,
  output Digit2D,
  output Digit3A,
  output Digit3B,
  output Digit3C,
  output Digit3D,
  output MemRef
);

  wire and_1_out, and_2_out, and_3_out, and_4_out, and_5_out, and_6_out, and_7_out, and_8_out, and_9_out,
       and_10_out, and_11_out, and_12_out, and_13_out, and_14_out, and_15_out, and_16_out, and_17_out,
       and_18_out, IO, not_1_out, Register;
  wire [4:0] driver_1_out, multiplexer_1_out;

  and and_1 (and_1_out, Register, IR[0]);
  and and_2 (and_2_out, Register, IR[1]);
  and and_3 (and_3_out, Register, IR[2]);
  and and_4 (and_4_out, Register, IR[3]);
  and and_5 (and_5_out, Register, IR[4]);
  and and_6 (and_6_out, Register, IR[5]);
  and and_7 (and_7_out, Register, IR[6]);
  and and_8 (and_8_out, Register, IR[7]);
  and and_9 (and_9_out, Register, IR[8]);
  and and_10 (and_10_out, Register, IR[9]);
  and and_11 (and_11_out, Register, IR[10]);
  and and_12 (and_12_out, Register, IR[11]);
  and and_13 (and_13_out, IO, IR[6]);
  and and_14 (and_14_out, IO, IR[7]);
  and and_15 (and_15_out, IO, IR[8]);
  and and_16 (and_16_out, IO, IR[9]);
  and and_17 (and_17_out, IO, IR[10]);
  and and_18 (and_18_out, IO, IR[11]);
  Multiplexer #(.Selector_Bits(3), .Bits(5)) multiplexer_1 (
    .sel(IR[14:12]), .in_0({5{1'b0}}), .in_1(5'b00001), .in_2(5'b00010), .in_3(5'b00011), .in_4(5'b00100),
    .in_5(5'b00101), .in_6(5'b00110), .in_7({5{1'b0}}), .out(multiplexer_1_out));
  nand nand_1 (MemRef, IR[14], IR[13], IR[12]);
  assign driver_1_out = and_1_out ? 5'b10010 : 5'bz;  // Driver driver_1
  assign driver_1_out = and_2_out ? 5'b10001 : 5'bz;  // Driver driver_2
  assign driver_1_out = and_3_out ? 5'b10000 : 5'bz;  // Driver driver_3
  assign driver_1_out = and_4_out ? 5'b01111 : 5'bz;  // Driver driver_4
  assign driver_1_out = and_5_out ? 5'b01110 : 5'bz;  // Driver driver_5
  assign driver_1_out = and_6_out ? 5'b01101 : 5'bz;  // Driver driver_6
  assign driver_1_out = and_7_out ? 5'b01100 : 5'bz;  // Driver driver_7
  assign driver_1_out = and_8_out ? 5'b01011 : 5'bz;  // Driver driver_8
  assign driver_1_out = and_9_out ? 5'b01010 : 5'bz;  // Driver driver_9
  assign driver_1_out = and_10_out ? 5'b01001 : 5'bz;  // Driver driver_10
  assign driver_1_out = and_11_out ? 5'b01000 : 5'bz;  // Driver driver_11
  assign driver_1_out = and_12_out ? 5'b00111 : 5'bz;  // Driver driver_12
  assign driver_1_out = and_13_out ? 5'b11000 : 5'bz;  // Driver driver_13
  assign driver_1_out = and_14_out ? 5'b10111 : 5'bz;  // Driver driver_14
  assign driver_1_out = and_15_out ? 5'b10110 : 5'bz;  // Driver driver_15
  assign driver_1_out = and_16_out ? 5'b10101 : 5'bz;  // Driver driver_16
  assign driver_1_out = and_17_out ? 5'b10100 : 5'bz;  // Driver driver_17
  assign driver_1_out = and_18_out ? 5'b10011 : 5'bz;  // Driver driver_18
  assign driver_1_out = MemRef ? multiplexer_1_out : 5'bz;  // Driver driver_19
  not not_1 (not_1_out, MemRef);
  and and_19 (IO, not_1_out, IR[15]);
  and and_20 (Indirect, MemRef, IR[15]);
  and and_21 (Register, ~IR[15], not_1_out);  // And
  ROM #(.AddrBits(5), .Bits(48)) rom_1 (.A(driver_1_out), .sel(1'b1), .D({Letter3, Letter2, Letter1}));
  and and_22 (Digit1A, MemRef, IR[8]);
  and and_23 (Digit1B, MemRef, IR[9]);
  and and_24 (Digit1C, MemRef, IR[10]);
  and and_25 (Digit1D, MemRef, IR[11]);
  and and_26 (Digit2A, MemRef, IR[4]);
  and and_27 (Digit2B, MemRef, IR[5]);
  and and_28 (Digit2C, MemRef, IR[6]);
  and and_29 (Digit2D, MemRef, IR[7]);
  and and_30 (Digit3A, MemRef, IR[0]);
  and and_31 (Digit3B, MemRef, IR[1]);
  and and_32 (Digit3C, MemRef, IR[2]);
  and and_33 (Digit3D, MemRef, IR[3]);

  // Other names for the same wires on the sheet: B_0 = IR[0]; B_1 = IR[1]; B_2 = IR[2]; B_3 = IR[3]; B_4 = IR[4];
  //   B_5 = IR[5]; B_6 = IR[6]; B_7 = IR[7]; B_8 = IR[8]; B_9 = IR[9]; B_10 = IR[10]; B_11 = IR[11]; I = IR[15]

  // Notes on the sheet:
  //   rom_1 loads 16-segment-letters.hex
endmodule
