// Digital circuit ControlUnit.dig as structural Verilog
module ControlUnit (
  input  [15:0] IR,
  input  CLK,
  input  S,
  input  R,
  input  I,
  input  IEN,
  input  FGI,
  input  E,
  input  [15:0] AC,
  input  [15:0] DR,
  input  [7:0] C_OUT,
  input  FGO,
  output S_CLR,
  output I_LD,
  output I_D,
  output R_J,
  output R_K,
  output IEN_J,
  output IEN_K,
  output FGI_K,
  output FGO_K,
  output AR_LD,
  output AR_INR,
  output AR_CLR,
  output MEM_read,
  output MEM_write,
  output PC_LD,
  output PC_INCR,
  output PC_CLR,
  output DR_LD,
  output DR_INCR,
  output AC_LD,
  output AC_INCR,
  output AC_CLR,
  output [6:0] AL_OP,
  output OUTR_LD,
  output IR_LD,
  output TR_LD,
  output [15:0] T,
  output [7:0] D,
  output E_J,
  output E_K,
  output [6:0] X
);

  wire ac_b6, ac_b7, ac_b9, AC_loadadd, AC_loadand, AC_Loadlda, AC_Sta, albit1, albit2, albit3, and_3_out,
       and_4_out, and_5_out, and_6_out, and_10_out, and_57_out, and_58_out, ar_bsa, ar_bun, AR_LD1, AR_load2,
       B0, B1, B2, B3, B4, B5, B6, B7, B8, B9, B10, B11, D0, D1, D2, D3, D4, D5, D6, D7, decoder_3_out_3,
       decoder_3_out_5, decoder_3_out_6, decoder_3_out_7, decoder_3_out_9, decoder_3_out_10,
       decoder_3_out_11, decoder_3_out_12, decoder_3_out_13, decoder_3_out_14, decoder_3_out_15,
       decoder_4_out_3, decoder_4_out_5, decoder_4_out_6, decoder_4_out_7, decoder_4_out_9, decoder_4_out_10,
       decoder_4_out_11, decoder_4_out_12, decoder_4_out_13, decoder_4_out_14, decoder_4_out_15,
       decoder_6_out_3, decoder_6_out_5, decoder_6_out_6, decoder_6_out_7, decoder_6_out_9, decoder_6_out_10,
       decoder_6_out_11, decoder_6_out_12, decoder_6_out_13, decoder_6_out_14, decoder_6_out_15, DR_loadadd,
       DR_loadand, DR_loadlda, drisz, drloadisz1, E_J1, E_J3, E_J4, E_K1, E_K2, E_K3, E_k4, IEN_K1, IEN_K2,
       IEN_K3, not_1_out, not_2_out, not_3_out, not_4_out, not_5_out, not_6_out, not_7_out, not_8_out,
       not_9_out, not_10_out, not_11_out, not_12_out, not_13_out, not_14_out, not_15_out, not_16_out,
       not_17_out, not_18_out, not_19_out, not_20_out, not_21_out, not_22_out, not_23_out, not_24_out,
       not_25_out, not_26_out, not_27_out, not_28_out, not_29_out, not_30_out, not_31_out, not_32_out,
       not_33_out, not_34_out, not_35_out, not_36_out, not_37_out, not_38_out, not_39_out, not_40_out,
       not_41_out, not_42_out, not_43_out, not_44_out, not_45_out, not_46_out, not_47_out, not_48_out,
       not_49_out, not_50_out, not_51_out, not_52_out, not_53_out, not_54_out, not_55_out, not_56_out,
       not_57_out, or_1_out, orta0, orta1, orta2, orta4, orta8, overflow, p, PC_INCRb1, PC_INCRb2, PC_INCRb3,
       PC_INCRb4, PC_INCRb8, PC_INCRb9, pcincisz, r_t, sag0, sag1, sag2, sag4, sag8, SC, sol0, sol1, sol2,
       sol4, sol8;
  wire [3:0] SC_out;

  Decoder #(.Selector_Bits(3)) decoder_1 (
    .sel(IR[14:12]), .out_0(D[0]), .out_1(D[1]), .out_2(D[2]), .out_3(D[3]), .out_4(D[4]), .out_5(D[5]),
    .out_6(D[6]), .out_7(D[7]));
  and and_1 (p, D7, I, T[3]);
  Counter #(.Bits(4)) u_SC (.en(S), .C(CLK), .clr(SC), .out(SC_out), .ovf(overflow));
  Decoder #(.Selector_Bits(3)) decoder_2 (
    .sel(IR[14:12]), .out_0(D0), .out_1(D1), .out_2(D2), .out_3(D3), .out_4(D4), .out_5(D5), .out_6(D6),
    .out_7(D7));
  Decoder #(.Selector_Bits(4)) decoder_3 (
    .sel(IR[11:8]), .out_0(sol0), .out_1(sol1), .out_2(sol2), .out_3(decoder_3_out_3), .out_4(sol4),
    .out_5(decoder_3_out_5), .out_6(decoder_3_out_6), .out_7(decoder_3_out_7), .out_8(sol8),
    .out_9(decoder_3_out_9), .out_10(decoder_3_out_10), .out_11(decoder_3_out_11), .out_12(decoder_3_out_12),
    .out_13(decoder_3_out_13), .out_14(decoder_3_out_14), .out_15(decoder_3_out_15));
  LED led_1 (.in(decoder_3_out_3));
  LED led_2 (.in(decoder_3_out_5));
  LED led_3 (.in(decoder_3_out_6));
  LED led_4 (.in(decoder_3_out_7));
  LED led_5 (.in(decoder_3_out_9));
  LED led_6 (.in(decoder_3_out_10));
  LED led_7 (.in(decoder_3_out_11));
  LED led_8 (.in(decoder_3_out_12));
  LED led_9 (.in(decoder_3_out_13));
  LED led_10 (.in(decoder_3_out_14));
  LED led_11 (.in(decoder_3_out_15));
  and and_2 (S_CLR, r_t, B0);
  and and_3 (and_3_out, r_t, B1);
  and and_4 (and_4_out, r_t, B2);
  and and_5 (and_5_out, r_t, B3);
  and and_6 (and_6_out, r_t, B4);
  and and_7 (AC_INCR, r_t, B5);
  and and_8 (ac_b6, r_t, B6);
  and and_9 (ac_b7, r_t, B7);
  and and_10 (and_10_out, r_t, B8);
  and and_11 (ac_b9, r_t, B9);
  and and_12 (E_K1, r_t, B10);
  and and_13 (AC_CLR, r_t, B11);
  Decoder #(.Selector_Bits(4)) decoder_4 (
    .sel(IR[7:4]), .out_0(orta0), .out_1(orta1), .out_2(orta2), .out_3(decoder_4_out_3), .out_4(orta4),
    .out_5(decoder_4_out_5), .out_6(decoder_4_out_6), .out_7(decoder_4_out_7), .out_8(orta8),
    .out_9(decoder_4_out_9), .out_10(decoder_4_out_10), .out_11(decoder_4_out_11), .out_12(decoder_4_out_12),
    .out_13(decoder_4_out_13), .out_14(decoder_4_out_14), .out_15(decoder_4_out_15));
  LED led_12 (.in(decoder_4_out_3));
  LED led_13 (.in(decoder_4_out_5));
  LED led_14 (.in(decoder_4_out_6));
  LED led_15 (.in(decoder_4_out_7));
  LED led_16 (.in(decoder_4_out_9));
  LED led_17 (.in(decoder_4_out_10));
  LED led_18 (.in(decoder_4_out_11));
  LED led_19 (.in(decoder_4_out_12));
  LED led_20 (.in(decoder_4_out_13));
  LED led_21 (.in(decoder_4_out_14));
  LED led_22 (.in(decoder_4_out_15));
  Decoder #(.Selector_Bits(4)) decoder_5 (
    .sel(SC_out), .out_0(T[0]), .out_1(T[1]), .out_2(T[2]), .out_3(T[3]), .out_4(T[4]), .out_5(T[5]),
    .out_6(T[6]), .out_7(T[7]), .out_8(T[8]), .out_9(T[9]), .out_10(T[10]), .out_11(T[11]), .out_12(T[12]),
    .out_13(T[13]), .out_14(T[14]), .out_15(T[15]));
  not not_1 (not_1_out, E);
  Decoder #(.Selector_Bits(4)) decoder_6 (
    .sel(IR[3:0]), .out_0(sag0), .out_1(sag1), .out_2(sag2), .out_3(decoder_6_out_3), .out_4(sag4),
    .out_5(decoder_6_out_5), .out_6(decoder_6_out_6), .out_7(decoder_6_out_7), .out_8(sag8),
    .out_9(decoder_6_out_9), .out_10(decoder_6_out_10), .out_11(decoder_6_out_11), .out_12(decoder_6_out_12),
    .out_13(decoder_6_out_13), .out_14(decoder_6_out_14), .out_15(decoder_6_out_15));
  not not_2 (not_2_out, I);
  and and_14 (PC_INCRb1, not_1_out, and_3_out);
  not not_3 (not_3_out, E);
  LED led_23 (.in(decoder_6_out_3));
  LED led_24 (.in(decoder_6_out_5));
  LED led_25 (.in(decoder_6_out_6));
  LED led_26 (.in(decoder_6_out_7));
  LED led_27 (.in(decoder_6_out_9));
  LED led_28 (.in(decoder_6_out_10));
  LED led_29 (.in(decoder_6_out_11));
  LED led_30 (.in(decoder_6_out_12));
  LED led_31 (.in(decoder_6_out_13));
  LED led_32 (.in(decoder_6_out_14));
  LED led_33 (.in(decoder_6_out_15));
  and and_15 (r_t, D7, not_2_out, T[3]);
  and and_16 (E_J1, not_3_out, and_10_out);
  and and_17 (E_K2, and_10_out, E);
  not not_4 (not_4_out, R);
  not not_5 (not_5_out, D7);
  not not_6 (not_6_out, T[0]);
  not not_7 (not_7_out, T[1]);
  not not_8 (not_8_out, T[2]);
  or or_1 (or_1_out, FGI, FGO);
  and and_18 (AR_CLR, R, T[0]);
  not not_9 (not_9_out, R);
  not not_10 (not_10_out, R);
  and and_19 (I_LD, not_4_out, T[2]);
  and and_20 (AR_load2, not_5_out, I, T[3]);
  and and_21 (R_J, not_6_out, not_7_out, not_8_out, IEN, or_1_out);
  and and_22 (PC_INCRb2, and_4_out, not_11_out, not_12_out, not_13_out, not_14_out, not_15_out, not_16_out, not_17_out, not_18_out, not_19_out, not_20_out, not_21_out, not_22_out, not_23_out, not_24_out, not_25_out, not_26_out);
  not not_11 (not_11_out, AC[0]);
  not not_12 (not_12_out, AC[1]);
  not not_13 (not_13_out, AC[2]);
  not not_14 (not_14_out, AC[3]);
  not not_15 (not_15_out, AC[4]);
  not not_16 (not_16_out, AC[5]);
  not not_17 (not_17_out, AC[6]);
  not not_18 (not_18_out, AC[7]);
  not not_19 (not_19_out, AC[8]);
  not not_20 (not_20_out, AC[9]);
  not not_21 (not_21_out, AC[10]);
  not not_22 (not_22_out, AC[11]);
  not not_23 (not_23_out, AC[12]);
  not not_24 (not_24_out, AC[13]);
  not not_25 (not_25_out, AC[14]);
  not not_26 (not_26_out, AC[15]);
  and and_23 (AR_LD1, T[0], not_9_out);
  and and_24 (IR_LD, T[1], not_10_out);
  and and_25 (B0, sag1, orta0, sol0);
  and and_26 (B1, sag2, orta0, sol0);
  and and_27 (B2, sag4, orta0, sol0);
  not not_27 (not_27_out, AC[0]);
  and and_28 (PC_CLR, T[1], R);
  and and_29 (IEN_K1, T[2], R);
  and and_30 (B3, sag8, orta0, sol0);
  and and_31 (E_J4, AC[0], ac_b7);
  and and_32 (E_k4, ac_b7, not_27_out);
  and and_33 (E_J3, ac_b6, AC[15]);
  and and_34 (E_K3, ac_b6, not_28_out);
  not not_28 (not_28_out, AC[15]);
  not not_29 (not_29_out, AC[15]);
  and and_35 (B4, sol0, sag0, orta1);
  and and_36 (B5, sol0, sag0, orta2);
  and and_37 (B6, sol0, sag0, orta4);
  and and_38 (B7, sol0, sag0, orta8);
  and and_39 (PC_INCRb3, and_5_out, AC[15], AC[15]);
  and and_40 (PC_INCRb4, not_29_out, not_29_out, and_6_out);
  and and_41 (DR_loadand, D0, T[4]);
  and and_42 (AC_loadand, D0, T[5]);
  and and_43 (B8, orta0, sol1, sag0);
  and and_44 (B9, orta0, sag0, sol2);
  and and_45 (B10, orta0, sol4, sag0);
  and and_46 (B11, orta0, sol8, sag0);
  or or_2 (E_K, E_K1, E_K2, E_K3, E_k4);
  and and_47 (DR_loadlda, D2, T[4]);
  and and_48 (AC_Loadlda, D2, T[5]);
  and and_49 (AC_Sta, D3, T[4]);
  or or_3 (E_J, E_J1, AC_loadadd, E_J3, E_J4);
  not not_30 (not_30_out, albit1);
  not not_31 (not_31_out, albit2);
  not not_32 (not_32_out, albit3);
  not not_33 (not_33_out, albit2);
  not not_34 (not_34_out, albit3);
  or or_4 (X[6], DR_loadand, drloadisz1, DR_loadlda, DR_loadadd, IR_LD, AR_load2);
  and and_50 (AL_OP[0], not_30_out, not_31_out, not_32_out);
  and and_51 (AL_OP[1], albit1, not_33_out, not_34_out);
  and and_52 (DR_loadadd, D1, T[4]);
  and and_53 (AC_loadadd, D1, T[5]);
  and and_54 (AC_loadadd, D1, T[5]);
  and and_55 (IEN_K2, p, B6);
  and and_56 (IEN_J, p, B7);
  and and_57 (and_57_out, p, B8);
  and and_58 (and_58_out, p, B9);
  and and_59 (FGO_K, p, B10);
  and and_60 (ar_bun, D4, T[4]);
  and and_61 (FGI_K, p, B11);
  or or_5 (X[3], ac_b6, ac_b7, FGO_K, ac_b9, AC_Sta);
  or or_6 (X[2], drisz, AC_Loadlda);
  or or_7 (PC_INCR, PC_INCRb1, PC_INCRb2, PC_INCRb3, IEN_K1, IR_LD, pcincisz, PC_INCRb4, PC_INCRb8, PC_INCRb9);
  not not_35 (not_35_out, albit1);
  not not_36 (not_36_out, albit3);
  not not_37 (not_37_out, albit3);
  and and_62 (PC_INCRb8, FGO, and_57_out);
  and and_63 (PC_INCRb9, and_58_out, FGI);
  or or_8 (MEM_read, DR_loadlda, drloadisz1, DR_loadand, IR_LD, AR_load2, DR_loadadd);
  or or_9 (DR_LD, drloadisz1, DR_loadadd, DR_loadand, AC_Loadlda, DR_loadlda);
  and and_64 (AL_OP[2], not_35_out, albit2, not_36_out);
  and and_65 (AL_OP[3], albit1, albit2, not_37_out);
  PriorityEncoder #(.Selector_Bits(3)) priorityencoder_1 (
    .in0(AC_loadand), .in1(AC_loadadd), .in2(AC_Loadlda), .in3(FGI_K), .in4(ac_b9), .in5(ac_b7), .in6(ac_b6),
    .in7(1'b0), .num({albit3, albit2, albit1}));  // open: any
  or or_10 (X[1], AR_LD1, AR_CLR, AR_INR);
  or or_11 (PC_LD, ar_bsa, ar_bun);
  or or_12 (MEM_write, AR_INR, drisz, PC_CLR, AC_Sta);
  or or_13 (AC_LD, AC_loadadd, AC_loadand, FGI_K, AC_Loadlda, ac_b9, ac_b7, ac_b6);
  and and_66 (AL_OP[4], not_38_out, not_39_out, albit3);
  not not_38 (not_38_out, albit1);
  not not_39 (not_39_out, albit2);
  and and_67 (AL_OP[5], albit1, not_40_out, albit3);
  not not_40 (not_40_out, albit2);
  and and_68 (AR_INR, D5, T[4]);
  and and_69 (ar_bsa, D5, T[5]);
  or or_14 (X[0], ar_bun, ar_bsa);
  and and_70 (AL_OP[6], not_41_out, albit2, albit3);
  not not_41 (not_41_out, albit1);
  or or_15 (SC, AC_Loadlda, ar_bun, IEN_K1, AC_Sta, AC_loadadd, drisz, ar_bsa, AC_loadand, p, r_t);
  or or_16 (IEN_K3, r_t, p);
  or or_17 (IEN_K, IEN_K2, IEN_K1, IEN_K3);
  and and_71 (drloadisz1, D6, T[4]);
  and and_72 (DR_INCR, D6, T[5]);
  and and_73 (drisz, D6, T[6]);
  or or_18 (AR_LD, AR_LD1, I_LD, AR_load2);
  or or_19 (R_K, IEN_K3, IEN_K1);
  and and_74 (pcincisz, drisz, not_42_out, not_43_out, not_44_out, not_45_out, not_46_out, not_47_out, not_48_out, not_49_out, not_50_out, not_51_out, not_52_out, not_53_out, not_54_out, not_55_out, not_56_out, not_57_out);
  not not_42 (not_42_out, DR[0]);
  not not_43 (not_43_out, DR[1]);
  not not_44 (not_44_out, DR[2]);
  not not_45 (not_45_out, DR[3]);
  not not_46 (not_46_out, DR[4]);
  not not_47 (not_47_out, DR[5]);
  not not_48 (not_48_out, DR[6]);
  not not_49 (not_49_out, DR[7]);
  not not_50 (not_50_out, DR[8]);
  not not_51 (not_51_out, DR[9]);
  not not_52 (not_52_out, DR[10]);
  not not_53 (not_53_out, DR[11]);
  not not_54 (not_54_out, DR[12]);
  not not_55 (not_55_out, DR[13]);
  not not_56 (not_56_out, DR[14]);
  not not_57 (not_57_out, DR[15]);

  assign I_D = IR[15];
  assign OUTR_LD = FGO_K;
  assign TR_LD = AR_CLR;
  assign X[5:4] = {PC_CLR, I_LD};

  // Other names for the same wires on the sheet: ac_loadcomp = ac_b9; AL_OP_COMb81 = ac_b9; ac_loadinp = FGI_K;
  //   AL_OP_INPR = FGI_K; ac_t = X[3]; ac_loadl = ac_b6; alop_shlb6 = ac_b6; ac_loadr = ac_b7; alop_shrb7 = ac_b7;
  //   PC_loadbun = ar_bun; SC_clrbun = ar_bun; at = FGO_K; dr_t = X[2]; drincisz = DR_INCR; sağ[3:0] = IR[3:0];
  //   orta[3:0] = IR[7:4]; sol[3:0] = IR[11:8]; AR_load1 = I_LD; IR_1 = I_LD; ir_t = I_LD; mem = X[6];
  //   MEM_2 = AR_load2; MEM_read2 = AR_load2; MEM_add = DR_loadadd; MEM_readadd = DR_loadadd; Mem_and = DR_loadand;
  //   Mem_readand = DR_loadand; MEM_lda = DR_loadlda; MEM_readlda = DR_loadlda; memisz = drloadisz1;
  //   memreadisz = drloadisz1; out0 = AL_OP[0]; out1 = AL_OP[1]; out2 = AL_OP[2]; out3 = AL_OP[3]; out4 = AL_OP[4];
  //   out5 = AL_OP[5]; out6 = AL_OP[6]; SC_pclr = p; pc = X[1]; PC_1 = AR_LD1; AR_clr1 = AR_CLR; PC_2 = AR_CLR;
  //   ar_incbsa = AR_INR; mem_writebsa = AR_INR; pc_bsa = AR_INR; MEM_1 = IR_LD; MEM_read1 = IR_LD; PC_inc1 = IR_LD;
  //   r_clr11 = PC_INCRb3; r_clr12 = PC_INCRb4; AC_INCRb5 = AC_INCR; r_clr13 = AC_INCR; r_clr14 = AC_CLR;
  //   R_K2 = IEN_K3; SC_rbclr = r_t; PC_inc2 = IEN_K1; R_K1 = IEN_K1; S_clr1 = IEN_K1; S_CLRr0 = S_CLR;
  //   ALOP_addadd = AC_loadadd; C_outadd = AC_loadadd; E_J2 = AC_loadadd; SC_clradd = AC_loadadd;
  //   ALOPandand = AC_loadand; SC_clrand = AC_loadand; pc_loadbsa = ar_bsa; sc_clrbsa = ar_bsa; AL_OP_DR = AC_Loadlda;
  //   DR_lda = AC_Loadlda; SC_clrlda = AC_Loadlda; MEM_writesta = AC_Sta; SC_clrsta = AC_Sta; memwriteisz = drisz;
  //   scclrisz = drisz; MEM_write1 = PC_CLR; PC_clr1 = PC_CLR; tr = PC_CLR; TR_1 = PC_CLR

  // Notes on the sheet:
  //   AC: default 100
  //   Outputs
  //   Inputs
  //   IR Processing
  //   p
  //   Register Reference
  //   r
  //   Fetch Phase
  //   Decoding
  //   Indirect
  //   Interrupt
  //   B
  //   Memory Reference
  //   And
  //   LDA
  //   STA
  //   I/O
  //   Add
  //   Bus
  //   BUN
  //   BSA
  //   ISZ
endmodule
