// Digital circuit I.dig as structural Verilog
module I (
  input  CLK,
  input  EN,
  input  D,
  output Q
);

  wire and_1_out, and_2_out, or_1_out;

  and and_1 (and_1_out, EN, D);
  and and_2 (and_2_out, ~EN, Q);  // And
  or or_1 (or_1_out, and_1_out, and_2_out);
  D_FF I (.D(or_1_out), .C(CLK), .Q(Q));  // open: nQ
endmodule
