// Digital circuit PC.dig as structural Verilog
module PC (
  input  CLR,
  input  [11:0] PIn,
  input  LD,
  input  INC,
  input  CLK,
  output [11:0] Out
);

  wire [11:0] add_1_s, multiplexer_1_out, multiplexer_2_out;

  Multiplexer #(.Bits(12)) multiplexer_1 (.sel(INC), .in_0(Out), .in_1(add_1_s), .out(multiplexer_1_out));
  Multiplexer #(.Bits(12)) multiplexer_2 (.sel(LD), .in_0(multiplexer_1_out), .in_1(PIn), .out(multiplexer_2_out));
  // Probe on multiplexer_2_out
  D_FF_AS #(.Bits(12)) PC (.Set(1'b0), .D(multiplexer_2_out), .C(CLK), .Clr(CLR), .Q(Out));  // open: nQ
  Add #(.Bits(12)) add_1 (.a(Out), .b(12'h1), .c_i(1'b0), .s(add_1_s));  // open: c_o
endmodule
