// Digital circuit SevenSegDecoderWithBlank.dig as structural Verilog
module SevenSegDecoderWithBlank (
  input  Blank,
  input  A_2,
  input  B_2,
  input  C_2,
  input  D_2,
  output g,
  output f,
  output e,
  output d,
  output c,
  output b,
  output a
);

  wire [6:0] rom_1_d;

  ROM #(.AddrBits(4), .Bits(7)) rom_1 (.A({D_2, C_2, B_2, A_2}), .sel(1'b1), .D(rom_1_d));
  assign {a, b, c, d, e, f, g} = {7{Blank}} & rom_1_d;  // And and_1, 7 bits wide

  // Notes on the sheet:
  //   contents of rom_1 (hex, n*v repeats v):
  //   7e,30,6d,79,33,5b,5f,70,7f,7b,77,1f,4e,3d,4f,47
endmodule
